# Fritzing sketch Circuit-Diagram (saved by Fritzing 0.9.8b)
breadboards: 1

parts:
  Mod1 = Raspberry Pi 4B
  R1 = Resistor [tolerance=±5% power=0.25 resistance=220 package=THT]
  LED1 = LED - 5mm [color="Red (633nm)" current=0.030 package="5 mm [THT]"]
  LED2 = LED - 5mm [color="Yellow (595nm)" current=0.030 package="5 mm [THT]"]
  R2 = Resistor [tolerance=±5% power=0.25 resistance=220 package=THT]
  R3 = Resistor [tolerance=±5% power=0.25 resistance=220 package=THT]
  LED3 = LED - 5mm [color="Green (555nm)" current=0.030 package="5 mm [THT]"]

nets:
  N1: Mod1.GPIO17, LED1.anode
  N2: Mod1.GPIO27, LED2.anode
  N3: Mod1.GND, R1.Pin_0, R2.Pin_0, R3.Pin_0
  N4: Mod1.GPIO22, LED3.anode
  N5: R1.Pin_1, LED1.cathode
  N6: LED2.cathode, R2.Pin_1
  N7: R3.Pin_1, LED3.cathode
